// Logisim project tes.circ as structural Verilog: 14 circuits, main circuit main
module main (
  input  CLR,
  output [31:0] Instr,
  output RegWrite,
  output [4:0] RegAddr,
  output [31:0] RegData,
  output MemWrite,
  output [4:0] MemAddr,
  output [31:0] MemData
);

  wire alu_1_zero, clock_1_out, control_1_bsel, control_1_wrsel;
  wire [1:0] control_1_npcop, control_1_wdsel;
  wire [2:0] control_1_extop;
  wire [3:0] control_1_aluop;
  wire [4:0] ifu_1_rd, ifu_1_rs, ifu_1_rt;
  wire [5:0] ifu_1_funct, ifu_1_opcode;
  wire [15:0] ifu_1_imm16;
  wire [31:0] alu_1_output, bsel_1_output, dm_1_output, ext_1_imm32, grf_1_rd1, ifu_1_pc4;

  Clock clock_1 (.out(clock_1_out));
  IFU ifu_1 (
    .TRI(clock_1_out), .CLR(CLR), .Instr(Instr), .funct(ifu_1_funct), .rd(ifu_1_rd), .rt(ifu_1_rt),
    .rs(ifu_1_rs), .opcode(ifu_1_opcode), .imm16(ifu_1_imm16), .PC4(ifu_1_pc4), .NPCOp(control_1_npcop),
    .Zero(alu_1_zero));  // open: shamt, imm26
  CONTROL control_1 (
    .RegWr(RegWrite), .DMWr(MemWrite), .ALUOp(control_1_aluop), .WrSel(control_1_wrsel),
    .WdSel(control_1_wdsel), .Bsel(control_1_bsel), .EXTOp(control_1_extop), .NPCOp(control_1_npcop),
    .opcode(ifu_1_opcode), .funct(ifu_1_funct));
  WrSel wrsel_1 (.Rd(ifu_1_rd), .Rt(ifu_1_rt), .out_4(RegAddr), .WdSel(control_1_wrsel));
  WdSel wdsel_1 (
    .ALU({alu_1_output[31:7], MemAddr, alu_1_output[1:0]}), .DM(dm_1_output), .PC4(ifu_1_pc4),
    .\output (RegData), .WdSel(control_1_wdsel));
  EXT ext_1 (.imm16(ifu_1_imm16), .imm32(ext_1_imm32), .EXTOp(control_1_extop));
  GRF grf_1 (
    .clk(clock_1_out), .reset(CLR), .RegWr(RegWrite), .A1(ifu_1_rs), .A2(ifu_1_rt), .RegAddr(RegAddr),
    .RegData(RegData), .RD1(grf_1_rd1), .RD2(MemData));
  Bsel bsel_1 (.ALU(MemData), .EXT(ext_1_imm32), .\output (bsel_1_output), .Bsel(control_1_bsel));
  ALU alu_1 (
    .A(grf_1_rd1), .B(bsel_1_output), .ALUOp(control_1_aluop),
    .\output ({alu_1_output[31:7], MemAddr, alu_1_output[1:0]}), .zero(alu_1_zero));
  DM dm_1 (
    .Address({alu_1_output[31:7], MemAddr, alu_1_output[1:0]}), .Data(MemData), .clk(clock_1_out), .clr(CLR),
    .\output (dm_1_output), .DMWr(MemWrite));

  // Other names for the same wires on the sheet: MemWr = MemWrite; RegWr = RegWrite
endmodule

module ALU (
  input  [31:0] A,
  input  [31:0] B,
  input  [3:0] ALUOp,
  output zero,
  output [31:0] \output 
);

  wire [31:0] adder_1_out, or_1_out, subtractor_1_out;

  Adder #(.width(32)) adder_1 (.a(A), .b(B), .out(adder_1_out));  // open: cin, cout
  Subtractor #(.width(32)) subtractor_1 (.a(A), .b(B), .out(subtractor_1_out));  // open: bin, bout
  assign or_1_out = A | B;  // OR_Gate or_1, 32 bits wide
  Comparator #(.width(32)) comparator_1 (.a(A), .b(B), .eq(zero));  // open: gt, lt
  Multiplexer #(.select(4), .width(32)) multiplexer_1 (
    .in1(adder_1_out), .in2(subtractor_1_out), .in4(or_1_out), .out(\output ), .sel(ALUOp));  // open: in0, in3, in5, in6, in7, in8, in9, in10, in11, in12, in13, in14, in15, en
endmodule

module GRF (
  input  clk,
  input  reset,
  input  RegWr,
  input  [4:0] A1,
  input  [4:0] A2,
  input  [4:0] RegAddr,
  input  [31:0] RegData,
  output [31:0] RD1,
  output [31:0] RD2
);

  wire [31:0] Rg0, Rg1, Rg2, Rg3, Rg4, Rg5, Rg6, Rg7, Rg8, Rg9, Rg10, Rg11, Rg12, Rg13, Rg14, Rg15, Rg16,
       Rg17, Rg18, Rg19, Rg20, Rg21, Rg22, Rg23, Rg24, Rg25, Rg26, Rg27, Rg28, Rg29, Rg30, Rg31, Wg1, Wg2,
       Wg3, Wg4, Wg5, Wg6, Wg7, Wg8, Wg9, Wg10, Wg11, Wg12, Wg13, Wg14, Wg15, Wg16, Wg17, Wg18, Wg19, Wg20,
       Wg21, Wg22, Wg23, Wg24, Wg25, Wg26, Wg27, Wg28, Wg29, Wg30, Wg31;

  Register #(.width(32)) register_1 (.D(Wg24), .en(RegWr), .Q(Rg24), .clk(clk), .clr(reset));
  Register #(.width(32)) register_2 (.D(Wg16), .en(RegWr), .Q(Rg16), .clk(clk), .clr(reset));
  Register #(.width(32)) register_3 (.D(Wg8), .en(RegWr), .Q(Rg8), .clk(clk), .clr(reset));
  Register #(.width(32)) register_4 (.Q(Rg0), .clk(clk), .clr(reset));  // open: D, en
  Multiplexer #(.select(5), .width(32)) multiplexer_1 (
    .in0(Rg0), .in1(Rg1), .in2(Rg2), .in3(Rg3), .in4(Rg4), .in5(Rg5), .in6(Rg6), .in7(Rg7), .in8(Rg8),
    .in9(Rg9), .in10(Rg10), .in11(Rg11), .in12(Rg12), .in13(Rg13), .in14(Rg14), .in15(Rg15), .in16(Rg16),
    .in17(Rg17), .in18(Rg18), .in19(Rg19), .in20(Rg20), .in21(Rg21), .in22(Rg22), .in23(Rg23), .in24(Rg24),
    .in25(Rg25), .in26(Rg26), .in27(Rg27), .in28(Rg28), .in29(Rg29), .in30(Rg30), .in31(Rg31), .out(RD1),
    .sel(A1));  // open: en
  Register #(.width(32)) register_5 (.D(Wg25), .en(RegWr), .Q(Rg25), .clk(clk), .clr(reset));
  Register #(.width(32)) register_6 (.D(Wg17), .en(RegWr), .Q(Rg17), .clk(clk), .clr(reset));
  Register #(.width(32)) register_7 (.D(Wg9), .en(RegWr), .Q(Rg9), .clk(clk), .clr(reset));
  Register #(.width(32)) register_8 (.D(Wg1), .en(RegWr), .Q(Rg1), .clk(clk), .clr(reset));
  Demultiplexer #(.select(5), .width(32), .tristate("true")) demultiplexer_1 (
    .out1(Wg1), .out2(Wg2), .out3(Wg3), .out4(Wg4), .out5(Wg5), .out6(Wg6), .out7(Wg7), .out8(Wg8),
    .out9(Wg9), .out10(Wg10), .out11(Wg11), .out12(Wg12), .out13(Wg13), .out14(Wg14), .out15(Wg15),
    .out16(Wg16), .out17(Wg17), .out18(Wg18), .out19(Wg19), .out20(Wg20), .out21(Wg21), .out22(Wg22),
    .out23(Wg23), .out24(Wg24), .out25(Wg25), .out26(Wg26), .out27(Wg27), .out28(Wg28), .out29(Wg29),
    .out30(Wg30), .out31(Wg31), .in(RegData), .sel(RegAddr));  // open: out0, en
  Register #(.width(32)) register_9 (.D(Wg26), .en(RegWr), .Q(Rg26), .clk(clk), .clr(reset));
  Register #(.width(32)) register_10 (.D(Wg18), .en(RegWr), .Q(Rg18), .clk(clk), .clr(reset));
  Register #(.width(32)) register_11 (.D(Wg10), .en(RegWr), .Q(Rg10), .clk(clk), .clr(reset));
  Register #(.width(32)) register_12 (.D(Wg2), .en(RegWr), .Q(Rg2), .clk(clk), .clr(reset));
  Register #(.width(32)) register_13 (.D(Wg27), .en(RegWr), .Q(Rg27), .clk(clk), .clr(reset));
  Register #(.width(32)) register_14 (.D(Wg19), .en(RegWr), .Q(Rg19), .clk(clk), .clr(reset));
  Register #(.width(32)) register_15 (.D(Wg11), .en(RegWr), .Q(Rg11), .clk(clk), .clr(reset));
  Register #(.width(32)) register_16 (.D(Wg3), .en(RegWr), .Q(Rg3), .clk(clk), .clr(reset));
  Register #(.width(32)) register_17 (.D(Wg28), .en(RegWr), .Q(Rg28), .clk(clk), .clr(reset));
  Register #(.width(32)) register_18 (.D(Wg20), .en(RegWr), .Q(Rg20), .clk(clk), .clr(reset));
  Register #(.width(32)) register_19 (.D(Wg12), .en(RegWr), .Q(Rg12), .clk(clk), .clr(reset));
  Register #(.width(32)) register_20 (.D(Wg4), .en(RegWr), .Q(Rg4), .clk(clk), .clr(reset));
  Register #(.width(32)) register_21 (.D(Wg29), .en(RegWr), .Q(Rg29), .clk(clk), .clr(reset));
  Register #(.width(32)) register_22 (.D(Wg21), .en(RegWr), .Q(Rg21), .clk(clk), .clr(reset));
  Register #(.width(32)) register_23 (.D(Wg13), .en(RegWr), .Q(Rg13), .clk(clk), .clr(reset));
  Register #(.width(32)) register_24 (.D(Wg5), .en(RegWr), .Q(Rg5), .clk(clk), .clr(reset));
  Register #(.width(32)) register_25 (.D(Wg30), .en(RegWr), .Q(Rg30), .clk(clk), .clr(reset));
  Register #(.width(32)) register_26 (.D(Wg22), .en(RegWr), .Q(Rg22), .clk(clk), .clr(reset));
  Register #(.width(32)) register_27 (.D(Wg14), .en(RegWr), .Q(Rg14), .clk(clk), .clr(reset));
  Register #(.width(32)) register_28 (.D(Wg6), .en(RegWr), .Q(Rg6), .clk(clk), .clr(reset));
  Register #(.width(32)) register_29 (.D(Wg31), .en(RegWr), .Q(Rg31), .clk(clk), .clr(reset));
  Register #(.width(32)) register_30 (.D(Wg23), .en(RegWr), .Q(Rg23), .clk(clk), .clr(reset));
  Register #(.width(32)) register_31 (.D(Wg15), .en(RegWr), .Q(Rg15), .clk(clk), .clr(reset));
  Register #(.width(32)) register_32 (.D(Wg7), .en(RegWr), .Q(Rg7), .clk(clk), .clr(reset));
  Multiplexer #(.select(5), .width(32)) multiplexer_2 (
    .in0(Rg0), .in1(Rg1), .in2(Rg2), .in3(Rg3), .in4(Rg4), .in5(Rg5), .in6(Rg6), .in7(Rg7), .in8(Rg8),
    .in9(Rg9), .in10(Rg10), .in11(Rg11), .in12(Rg12), .in13(Rg13), .in14(Rg14), .in15(Rg15), .in16(Rg16),
    .in17(Rg17), .in18(Rg18), .in19(Rg19), .in20(Rg20), .in21(Rg21), .in22(Rg22), .in23(Rg23), .in24(Rg24),
    .in25(Rg25), .in26(Rg26), .in27(Rg27), .in28(Rg28), .in29(Rg29), .in30(Rg30), .in31(Rg31), .out(RD2),
    .sel(A2));  // open: en

  // Other names for the same wires on the sheet: A3[4:0] = RegAddr; WD[31:0] = RegData
endmodule

module IM (
  input  [31:0] in_1,
  output [31:0] Instr,
  output [5:0] funct,
  output [4:0] shamt,
  output [4:0] rd,
  output [4:0] rt,
  output [4:0] rs,
  output [5:0] opcode,
  output [15:0] imm16,
  output [25:0] imm26
);

  ROM #(.addrWidth(5), .dataWidth(32)) rom_1 (
    .addr(in_1[6:2]), .data({Instr[31:26], imm26[25:16], imm16[15:6], funct}));  // open: sel

  assign imm16[5:0] = funct;
  assign imm26[15:0] = {imm16[15:6], funct};
  assign Instr[25:0] = {imm26[25:16], imm16[15:6], funct};
  assign opcode = Instr[31:26];
  assign rd = imm16[15:11];
  assign rs = imm26[25:21];
  assign rt = imm26[20:16];
  assign shamt = imm16[10:6];

  // Notes on the sheet:
  //   contents of rom_1 (hex, n*v repeats v):
  //   341c0000 341d0000 34013456 210820 8c010004 ac010004 3c027878 411822 3c051234 34040005 0 ac85ffff
  //   8c83ffff 10650001 1000000d 34670404 10e3000b 0 3c087777 3508ffff 80022 34001100 e65020 34080000
  //   34090001 340a0001 10a4020 1109fffe 1000ffff
endmodule

module DM (
  input  [31:0] Address,
  input  [31:0] Data,
  input  clk,
  input  clr,
  input  DMWr,
  output [31:0] \output 
);

  RAM #(.addrWidth(5), .dataWidth(32), .bus("separate")) ram_1 (
    .addr(Address[6:2]), .din(Data), .data(\output ), .str(DMWr), .clk(clk), .clr(clr));  // open: sel, ld
endmodule

module PC (
  input  [31:0] NPC,
  input  TRI,
  input  CLR,
  output [31:0] PC
);

  Register #(.width(32)) register_1 (.D(NPC), .Q(PC), .clk(TRI), .clr(CLR));  // open: en
endmodule

module IFU (
  input  TRI,
  input  CLR,
  input  [1:0] NPCOp,
  input  Zero,
  output [31:0] Instr,
  output [5:0] funct,
  output [4:0] shamt,
  output [4:0] rd,
  output [4:0] rt,
  output [4:0] rs,
  output [5:0] opcode,
  output [15:0] imm16,
  output [25:0] imm26,
  output [31:0] PC4
);

  wire [31:0] NPC_npc, pc_pc;

  NPC NPC (.in_1(pc_pc), .imm16(imm16), .imm26(imm26), .NPCOp(NPCOp), .zero(Zero), .PC4(PC4), .NPC(NPC_npc));
  PC pc (.NPC(NPC_npc), .TRI(TRI), .CLR(CLR), .PC(pc_pc));
  IM im_1 (
    .in_1(pc_pc), .Instr(Instr), .funct(funct), .shamt(shamt), .rd(rd), .rt(rt), .rs(rs), .opcode(opcode),
    .imm16(imm16), .imm26(imm26));
endmodule

module NPC (
  input  [31:0] in_1,
  input  [15:0] imm16,
  input  [25:0] imm26,
  input  [1:0] NPCOp,
  input  zero,
  output [31:0] PC4,
  output [31:0] NPC
);

  wire [15:0] shifter_1_out;
  wire [31:0] adder_2_out, bit_extender_1_out, bit_extender_2_out, multiplexer_1_out, shifter_2_out;

  Shifter #(.width(16)) shifter_1 (.in(imm16), .\dist (4'b0010), .out(shifter_1_out));
  assign bit_extender_1_out = {{2{1'b0}}, {in_1[31:28], imm26}};  // Bit_Extender bit_extender_1
  assign bit_extender_2_out = {{16{1'b0}}, shifter_1_out};  // Bit_Extender bit_extender_2
  Shifter #(.width(32)) shifter_2 (.in(bit_extender_1_out), .\dist (5'b00010), .out(shifter_2_out));
  Adder #(.width(32)) adder_1 (.a(in_1), .b(32'h4), .out(PC4));  // open: cin, cout
  Adder #(.width(32)) adder_2 (.a(PC4), .b(bit_extender_2_out), .out(adder_2_out));  // open: cin, cout
  Multiplexer #(.width(32)) multiplexer_1 (
    .in0(PC4), .in1(adder_2_out), .out(multiplexer_1_out), .sel(zero));  // open: en
  Multiplexer #(.select(2), .width(32)) multiplexer_2 (
    .in0(PC4), .in1(multiplexer_1_out), .in2(shifter_2_out), .out(NPC), .sel(NPCOp));  // open: in3, en
endmodule

module CONTROL (
  input  [5:0] funct,
  input  [5:0] opcode,
  output RegWr,
  output DMWr,
  output [3:0] ALUOp,
  output WrSel,
  output [1:0] WdSel,
  output Bsel,
  output [2:0] EXTOp,
  output [1:0] NPCOp
);

  wire ADD_out, and_1_out, and_2_out, and_3_out, J_out, not_1_out, not_2_out, not_3_out, not_4_out,
       not_5_out, not_6_out, not_7_out, not_8_out, not_9_out, not_10_out, not_11_out, not_12_out, not_13_out,
       not_14_out, not_15_out, not_16_out, not_17_out, not_18_out, not_19_out, not_20_out, not_21_out,
       not_22_out, not_23_out, not_24_out, not_25_out, not_26_out, not_27_out, not_28_out, not_29_out,
       not_30_out, not_31_out, not_32_out, not_33_out, not_34_out, not_35_out, not_36_out, not_37_out,
       not_38_out, not_39_out, or_6_out;

  not not_1 (not_1_out, funct[0]);
  not not_2 (not_2_out, funct[1]);
  not not_3 (not_3_out, funct[2]);
  not not_4 (not_4_out, funct[3]);
  not not_5 (not_5_out, funct[4]);
  not not_6 (not_6_out, opcode[0]);
  not not_7 (not_7_out, opcode[1]);
  not not_8 (not_8_out, opcode[2]);
  not not_9 (not_9_out, opcode[3]);
  not not_10 (not_10_out, opcode[4]);
  not not_11 (not_11_out, opcode[5]);
  not not_12 (not_12_out, funct[0]);
  not not_13 (not_13_out, funct[2]);
  not not_14 (not_14_out, funct[3]);
  not not_15 (not_15_out, funct[4]);
  not not_16 (not_16_out, opcode[0]);
  not not_17 (not_17_out, opcode[1]);
  not not_18 (not_18_out, opcode[3]);
  not not_19 (not_19_out, opcode[4]);
  not not_20 (not_20_out, opcode[5]);
  not not_21 (not_21_out, opcode[2]);
  not not_22 (not_22_out, opcode[3]);
  not not_23 (not_23_out, opcode[4]);
  not not_24 (not_24_out, opcode[2]);
  not not_25 (not_25_out, opcode[4]);
  not not_26 (not_26_out, opcode[1]);
  not not_27 (not_27_out, opcode[4]);
  not not_28 (not_28_out, opcode[5]);
  not not_29 (not_29_out, opcode[4]);
  not not_30 (not_30_out, opcode[5]);
  not not_31 (not_31_out, opcode[0]);
  not not_32 (not_32_out, opcode[2]);
  not not_33 (not_33_out, opcode[3]);
  not not_34 (not_34_out, opcode[4]);
  not not_35 (not_35_out, opcode[5]);
  not not_36 (not_36_out, opcode[2]);
  not not_37 (not_37_out, opcode[3]);
  not not_38 (not_38_out, opcode[4]);
  not not_39 (not_39_out, opcode[5]);
  and and_1 (and_1_out, not_1_out, not_2_out, not_3_out, not_4_out, not_5_out, funct[5]);
  and and_2 (and_2_out, not_6_out, not_7_out, not_8_out, not_9_out, not_10_out, not_11_out);
  and and_3 (and_3_out, not_12_out, funct[1], not_13_out, not_14_out, not_15_out, funct[5]);
  and ADD (ADD_out, and_1_out, and_2_out);
  and SUB (ALUOp[1], and_2_out, and_3_out);
  and BEQ (ALUOp[3], not_16_out, not_17_out, opcode[2], not_18_out, not_19_out, not_20_out);
  and LW (WdSel[0], opcode[0], opcode[1], not_21_out, not_22_out, not_23_out, opcode[5]);
  and SW (DMWr, opcode[0], opcode[1], not_24_out, opcode[3], not_25_out, opcode[5]);
  and ORI (EXTOp[0], opcode[0], not_26_out, opcode[2], opcode[3], not_27_out, not_28_out);
  and LUI (EXTOp[2], opcode[0], opcode[1], opcode[2], opcode[3], not_29_out, not_30_out);
  and J (J_out, not_31_out, opcode[1], not_32_out, not_33_out, not_34_out, not_35_out);
  and JAL (WdSel[1], opcode[0], opcode[1], not_36_out, not_37_out, not_38_out, not_39_out);
  or or_1 (ALUOp[0], ADD_out, WdSel[0], DMWr);
  or or_2 (ALUOp[2], EXTOp[0], EXTOp[2]);
  or or_3 (WrSel, EXTOp[2], EXTOp[0], WdSel[0]);
  or or_4 (Bsel, EXTOp[2], EXTOp[0], DMWr, WdSel[0]);
  or or_5 (EXTOp[1], WdSel[0], DMWr);
  or or_6 (or_6_out, ADD_out, ALUOp[1], WdSel[0], EXTOp[0], EXTOp[2]);
  or or_7 (NPCOp[1], J_out, WdSel[1]);
  or or_8 (RegWr, or_6_out, WdSel[1]);

  assign NPCOp[0] = ALUOp[3];
endmodule

module EXT (
  input  [15:0] imm16,
  input  [2:0] EXTOp,
  output [31:0] imm32
);

  wire [31:0] bit_extender_1_out, bit_extender_2_out, shifter_1_out;

  assign bit_extender_1_out = {{16{1'b0}}, imm16};  // Bit_Extender bit_extender_1
  assign bit_extender_2_out = {{16{imm16[15]}}, imm16};  // Bit_Extender bit_extender_2
  Shifter #(.width(32)) shifter_1 (.in(bit_extender_2_out), .\dist (5'b10000), .out(shifter_1_out));
  Multiplexer #(.select(3), .width(32)) multiplexer_1 (
    .in1(bit_extender_1_out), .in2(bit_extender_2_out), .in4(shifter_1_out), .out(imm32), .sel(EXTOp));  // open: in0, in3, in5, in6, in7, en
endmodule

module test (
  output [31:0] out_1,
  output out_2,
  output [4:0] out_3,
  output [31:0] out_4,
  output out_5,
  output out_6,
  output [4:0] out_7,
  output [31:0] out_8
);

  wire clock_1_out, comparator_1_gt;
  wire [7:0] counter_1_q;

  Clock clock_1 (.out(clock_1_out));
  Counter counter_1 (.Q(counter_1_q), .carry(out_5), .clk(clock_1_out));  // open: load, D, count, clr
  Comparator comparator_1 (.a(8'h4), .b(counter_1_q), .gt(comparator_1_gt));  // open: eq, lt
  main main_1 (
    .CLR(comparator_1_gt), .Instr(out_1), .RegWrite(out_2), .RegAddr(out_3), .RegData(out_4),
    .MemWrite(out_6), .MemAddr(out_7), .MemData(out_8));
endmodule

module WrSel (
  input  [4:0] Rd,
  input  [4:0] Rt,
  input  WdSel,
  output [4:0] out_4
);

  Multiplexer #(.width(5)) multiplexer_1 (.in0(Rd), .in1(Rt), .out(out_4), .sel(WdSel));  // open: en
endmodule

module WdSel (
  input  [31:0] ALU,
  input  [31:0] DM,
  input  [1:0] WdSel,
  input  [31:0] PC4,
  output [31:0] \output 
);

  Multiplexer #(.select(2), .width(32)) multiplexer_1 (
    .in0(ALU), .in1(DM), .in2(PC4), .out(\output ), .sel(WdSel));  // open: in3, en
endmodule

module Bsel (
  input  [31:0] ALU,
  input  [31:0] EXT,
  input  Bsel,
  output [31:0] \output 
);

  Multiplexer #(.width(32)) multiplexer_1 (.in0(ALU), .in1(EXT), .out(\output ), .sel(Bsel));  // open: en
endmodule
