// Logisim project crc.circ as structural Verilog: 2 circuits, main circuit 4bit2mod
module _4bit2mod (
  input  [3:0] A,
  input  [3:0] B,
  output [2:0] C
);

  wire and_1_out, and_2_out, and_3_out, and_4_out;

  and and_1 (and_1_out, B[0], and_4_out);
  and and_2 (and_2_out, B[1], and_4_out);
  and and_3 (and_3_out, B[2], and_4_out);
  and and_4 (and_4_out, A[3], B[3]);
  xor xor_1 (C[0], A[0], and_1_out);
  xor xor_2 (C[2], A[2], and_3_out);
  xor xor_3 (C[1], A[1], and_2_out);
endmodule

module CRC (
  input  [7:0] A,
  input  [3:0] B,
  output [10:0] C
);

  wire [2:0] n4bit2mod_1_c, n4bit2mod_2_c, n4bit2mod_3_c, n4bit2mod_4_c, n4bit2mod_5_c, n4bit2mod_6_c,
       n4bit2mod_7_c;

  _4bit2mod u_4bit2mod_1 (.A(A[7:4]), .B(B), .C(n4bit2mod_1_c));
  _4bit2mod u_4bit2mod_2 (.A({n4bit2mod_1_c, A[3]}), .B(B), .C(n4bit2mod_2_c));
  _4bit2mod u_4bit2mod_3 (.A({n4bit2mod_2_c, A[2]}), .B(B), .C(n4bit2mod_3_c));
  _4bit2mod u_4bit2mod_4 (.A({n4bit2mod_3_c, A[1]}), .B(B), .C(n4bit2mod_4_c));
  _4bit2mod u_4bit2mod_5 (.A({n4bit2mod_4_c, A[0]}), .B(B), .C(n4bit2mod_5_c));
  _4bit2mod u_4bit2mod_6 (.A({n4bit2mod_5_c, 1'b0}), .B(B), .C(n4bit2mod_6_c));
  _4bit2mod u_4bit2mod_7 (.A({n4bit2mod_6_c, 1'b0}), .B(B), .C(n4bit2mod_7_c));
  _4bit2mod u_4bit2mod_8 (.A({n4bit2mod_7_c, 1'b0}), .B(B), .C(C[2:0]));

  assign C[10:3] = A;
endmodule
