// Logisim project fsm.circ as structural Verilog: 3 circuits, main circuit fsm
module fsm (
  input  clr,
  input  [1:0] In,
  output out_3
);

  wire clock_1_out;
  wire [1:0] multiplexer_1_out, register_1_q, status_zhuanyi_1_ns1;

  Clock clock_1 (.out(clock_1_out));
  status_zhuanyi status_zhuanyi_1 (
    .s0(register_1_q[1]), .s1(register_1_q[0]), .in0(In[1]), .in1(In[0]), .NS0(status_zhuanyi_1_ns1[1]),
    .NS1(status_zhuanyi_1_ns1[0]), .Z(out_3));
  Register #(.width(2)) register_1 (.D(multiplexer_1_out), .Q(register_1_q), .clk(clock_1_out));  // open: en, clr
  Multiplexer #(.width(2)) multiplexer_1 (
    .in0(status_zhuanyi_1_ns1), .in1(2'b00), .out(multiplexer_1_out), .sel(clr));  // open: en
endmodule

module status_zhuanyi (
  input  s0,
  input  s1,
  input  in0,
  input  in1,
  output NS0,
  output NS1,
  output Z
);

  wire and_1_out, and_2_out, and_3_out, and_4_out, not_1_out, not_2_out, not_3_out, not_4_out, not_5_out,
       not_6_out, not_7_out, not_8_out, not_9_out;

  not not_1 (not_1_out, s0);
  and and_1 (and_1_out, not_1_out, s1, not_2_out);
  not not_2 (not_2_out, in1);
  not not_3 (not_3_out, s1);
  and and_2 (and_2_out, s0, not_3_out, not_4_out);
  not not_4 (not_4_out, in1);
  not not_5 (not_5_out, in0);
  and and_3 (and_3_out, not_5_out, in1);
  and and_4 (and_4_out, s0, not_6_out, not_7_out);
  not not_6 (not_6_out, s1);
  not not_7 (not_7_out, in1);
  and and_5 (Z, s0, not_8_out, not_9_out);
  not not_8 (not_8_out, s1);
  not not_9 (not_9_out, in1);
  or or_1 (NS0, and_1_out, and_2_out);
  or or_2 (NS1, and_3_out, and_4_out);
endmodule

module tes (
  output out_1,
  output [1:0] out_2,
  output out_3,
  output out_4
);

  wire clock_1_out;
  wire [7:0] counter_1_q;

  Counter counter_1 (.Q(counter_1_q), .carry(out_4), .clk(clock_1_out));  // open: load, D, count, clr
  Clock clock_1 (.out(clock_1_out));
  ROM #(.dataWidth(3)) rom_1 (.addr(counter_1_q), .data({out_2, out_1}));  // open: sel
  fsm fsm_1 (.clr(out_1), .In(out_2), .out_3(out_3));

  // Notes on the sheet:
  //   contents of rom_1 (hex, n*v repeats v):
  //   6*2 6*4 2 4 1 4 4 4 2 0 1 4 2 4 4
endmodule
