// Logisim project grf.circ as structural Verilog: 1 circuit, main circuit grf
module grf (
  input  clk,
  input  reset,
  input  RegWrite,
  input  [4:0] A1,
  input  [4:0] A2,
  input  [4:0] A3,
  input  [31:0] WD,
  output [31:0] RD1,
  output [31:0] RD2
);

  wire [31:0] Rg0, Rg1, Rg2, Rg3, Rg4, Rg5, Rg6, Rg7, Rg8, Rg9, Rg10, Rg11, Rg12, Rg13, Rg14, Rg15, Rg16,
       Rg17, Rg18, Rg19, Rg20, Rg21, Rg22, Rg23, Rg24, Rg25, Rg26, Rg27, Rg28, Rg29, Rg30, Rg31, Wg1, Wg2,
       Wg3, Wg4, Wg5, Wg6, Wg7, Wg8, Wg9, Wg10, Wg11, Wg12, Wg13, Wg14, Wg15, Wg16, Wg17, Wg18, Wg19, Wg20,
       Wg21, Wg22, Wg23, Wg24, Wg25, Wg26, Wg27, Wg28, Wg29, Wg30, Wg31;

  Register #(.width(32)) register_1 (.D(Wg24), .en(RegWrite), .Q(Rg24), .clk(clk), .clr(reset));
  Register #(.width(32)) register_2 (.D(Wg16), .en(RegWrite), .Q(Rg16), .clk(clk), .clr(reset));
  Register #(.width(32)) register_3 (.D(Wg8), .en(RegWrite), .Q(Rg8), .clk(clk), .clr(reset));
  Register #(.width(32)) register_4 (.Q(Rg0), .clk(clk), .clr(reset));  // open: D, en
  Multiplexer #(.select(5), .width(32)) multiplexer_1 (
    .in0(Rg0), .in1(Rg1), .in2(Rg2), .in3(Rg3), .in4(Rg4), .in5(Rg5), .in6(Rg6), .in7(Rg7), .in8(Rg8),
    .in9(Rg9), .in10(Rg10), .in11(Rg11), .in12(Rg12), .in13(Rg13), .in14(Rg14), .in15(Rg15), .in16(Rg16),
    .in17(Rg17), .in18(Rg18), .in19(Rg19), .in20(Rg20), .in21(Rg21), .in22(Rg22), .in23(Rg23), .in24(Rg24),
    .in25(Rg25), .in26(Rg26), .in27(Rg27), .in28(Rg28), .in29(Rg29), .in30(Rg30), .in31(Rg31), .out(RD1),
    .sel(A1));  // open: en
  Register #(.width(32)) register_5 (.D(Wg25), .en(RegWrite), .Q(Rg25), .clk(clk), .clr(reset));
  Register #(.width(32)) register_6 (.D(Wg17), .en(RegWrite), .Q(Rg17), .clk(clk), .clr(reset));
  Register #(.width(32)) register_7 (.D(Wg9), .en(RegWrite), .Q(Rg9), .clk(clk), .clr(reset));
  Register #(.width(32)) register_8 (.D(Wg1), .en(RegWrite), .Q(Rg1), .clk(clk), .clr(reset));
  Demultiplexer #(.select(5), .width(32), .tristate("true")) demultiplexer_1 (
    .out1(Wg1), .out2(Wg2), .out3(Wg3), .out4(Wg4), .out5(Wg5), .out6(Wg6), .out7(Wg7), .out8(Wg8),
    .out9(Wg9), .out10(Wg10), .out11(Wg11), .out12(Wg12), .out13(Wg13), .out14(Wg14), .out15(Wg15),
    .out16(Wg16), .out17(Wg17), .out18(Wg18), .out19(Wg19), .out20(Wg20), .out21(Wg21), .out22(Wg22),
    .out23(Wg23), .out24(Wg24), .out25(Wg25), .out26(Wg26), .out27(Wg27), .out28(Wg28), .out29(Wg29),
    .out30(Wg30), .out31(Wg31), .in(WD), .sel(A3));  // open: out0, en
  Register #(.width(32)) register_9 (.D(Wg26), .en(RegWrite), .Q(Rg26), .clk(clk), .clr(reset));
  Register #(.width(32)) register_10 (.D(Wg18), .en(RegWrite), .Q(Rg18), .clk(clk), .clr(reset));
  Register #(.width(32)) register_11 (.D(Wg10), .en(RegWrite), .Q(Rg10), .clk(clk), .clr(reset));
  Register #(.width(32)) register_12 (.D(Wg2), .en(RegWrite), .Q(Rg2), .clk(clk), .clr(reset));
  Register #(.width(32)) register_13 (.D(Wg27), .en(RegWrite), .Q(Rg27), .clk(clk), .clr(reset));
  Register #(.width(32)) register_14 (.D(Wg19), .en(RegWrite), .Q(Rg19), .clk(clk), .clr(reset));
  Register #(.width(32)) register_15 (.D(Wg11), .en(RegWrite), .Q(Rg11), .clk(clk), .clr(reset));
  Register #(.width(32)) register_16 (.D(Wg3), .en(RegWrite), .Q(Rg3), .clk(clk), .clr(reset));
  Register #(.width(32)) register_17 (.D(Wg28), .en(RegWrite), .Q(Rg28), .clk(clk), .clr(reset));
  Register #(.width(32)) register_18 (.D(Wg20), .en(RegWrite), .Q(Rg20), .clk(clk), .clr(reset));
  Register #(.width(32)) register_19 (.D(Wg12), .en(RegWrite), .Q(Rg12), .clk(clk), .clr(reset));
  Register #(.width(32)) register_20 (.D(Wg4), .en(RegWrite), .Q(Rg4), .clk(clk), .clr(reset));
  Register #(.width(32)) register_21 (.D(Wg29), .en(RegWrite), .Q(Rg29), .clk(clk), .clr(reset));
  Register #(.width(32)) register_22 (.D(Wg21), .en(RegWrite), .Q(Rg21), .clk(clk), .clr(reset));
  Register #(.width(32)) register_23 (.D(Wg13), .en(RegWrite), .Q(Rg13), .clk(clk), .clr(reset));
  Register #(.width(32)) register_24 (.D(Wg5), .en(RegWrite), .Q(Rg5), .clk(clk), .clr(reset));
  Register #(.width(32)) register_25 (.D(Wg30), .en(RegWrite), .Q(Rg30), .clk(clk), .clr(reset));
  Register #(.width(32)) register_26 (.D(Wg22), .en(RegWrite), .Q(Rg22), .clk(clk), .clr(reset));
  Register #(.width(32)) register_27 (.D(Wg14), .en(RegWrite), .Q(Rg14), .clk(clk), .clr(reset));
  Register #(.width(32)) register_28 (.D(Wg6), .en(RegWrite), .Q(Rg6), .clk(clk), .clr(reset));
  Register #(.width(32)) register_29 (.D(Wg31), .en(RegWrite), .Q(Rg31), .clk(clk), .clr(reset));
  Register #(.width(32)) register_30 (.D(Wg23), .en(RegWrite), .Q(Rg23), .clk(clk), .clr(reset));
  Register #(.width(32)) register_31 (.D(Wg15), .en(RegWrite), .Q(Rg15), .clk(clk), .clr(reset));
  Register #(.width(32)) register_32 (.D(Wg7), .en(RegWrite), .Q(Rg7), .clk(clk), .clr(reset));
  Multiplexer #(.select(5), .width(32)) multiplexer_2 (
    .in0(Rg0), .in1(Rg1), .in2(Rg2), .in3(Rg3), .in4(Rg4), .in5(Rg5), .in6(Rg6), .in7(Rg7), .in8(Rg8),
    .in9(Rg9), .in10(Rg10), .in11(Rg11), .in12(Rg12), .in13(Rg13), .in14(Rg14), .in15(Rg15), .in16(Rg16),
    .in17(Rg17), .in18(Rg18), .in19(Rg19), .in20(Rg20), .in21(Rg21), .in22(Rg22), .in23(Rg23), .in24(Rg24),
    .in25(Rg25), .in26(Rg26), .in27(Rg27), .in28(Rg28), .in29(Rg29), .in30(Rg30), .in31(Rg31), .out(RD2),
    .sel(A2));  // open: en
endmodule
