// Logisim project main.circ as structural Verilog: 1 circuit, main circuit main
module main (
  input  [2:0] in_1,
  output [3:0] Nth
);

  wire clk, comparator_1_eq, comparator_2_eq, comparator_3_eq, comparator_4_eq, not_1_out;
  wire [3:0] adder_1_out, multiplexer_1_out, multiplexer_2_out, multiplexer_3_out, register_1_q,
       register_2_q, register_3_q;
  wire [6:0] bit_extender_1_out, counter_1_q;

  Multiplexer #(.width(4)) multiplexer_1 (
    .in0(register_3_q), .in1(4'b0001), .out(multiplexer_1_out), .sel(comparator_1_eq));  // open: en
  Comparator #(.width(4)) comparator_1 (.a(4'b0000), .b(register_1_q), .eq(comparator_1_eq));  // open: gt, lt
  Clock clock_1 (.out(clk));
  Register #(.width(4)) register_1 (.D(multiplexer_1_out), .Q(register_1_q), .clk(clk));  // open: en, clr
  Register #(.width(4)) register_2 (.D(register_1_q), .Q(register_2_q), .clk(clk));  // open: en, clr
  Counter #(.width(7), .max('h7f)) counter_1 (.Q(counter_1_q), .clk(clk));  // open: load, D, count, carry, clr
  assign bit_extender_1_out = {{4{1'b0}}, in_1};  // Bit_Extender bit_extender_1
  Adder #(.width(4)) adder_1 (.a(register_1_q), .b(register_2_q), .out(adder_1_out));  // open: cin, cout
  Comparator #(.width(7)) comparator_2 (.a(bit_extender_1_out), .b(counter_1_q), .eq(comparator_2_eq));  // open: gt, lt
  Register #(.width(4)) register_3 (.D(adder_1_out), .Q(register_3_q), .clk(not_1_out));  // open: en, clr
  not not_1 (not_1_out, clk);
  Multiplexer #(.width(4)) multiplexer_2 (
    .in0(register_3_q), .in1(4'b0001), .out(multiplexer_2_out), .sel(comparator_3_eq));  // open: en
  Comparator #(.width(3)) comparator_3 (.a(in_1), .b(3'b001), .eq(comparator_3_eq));  // open: gt, lt
  Comparator #(.width(3)) comparator_4 (.a(in_1), .b(3'b010), .eq(comparator_4_eq));  // open: gt, lt
  Multiplexer #(.width(4)) multiplexer_3 (
    .in0(multiplexer_2_out), .in1(4'b0001), .out(multiplexer_3_out), .sel(comparator_4_eq));  // open: en
  Register #(.width(4)) register_4 (.D(multiplexer_3_out), .Q(Nth), .clk(comparator_2_eq));  // open: en, clr

  // Other names for the same wires on the sheet: in[2:0] = in_1
endmodule
