// Logisim project mod5.circ as structural Verilog: 3 circuits, main circuit mod5
module mod5 (
  input  in_1,
  output s0,
  output out_3,
  output out_4,
  output out_5,
  output out_6
);

  wire clock_1_out;
  wire [1:0] register_1_q, status_zhuanyi_1_ns1;

  Clock clock_1 (.out(clock_1_out));
  status_zhuanyi status_zhuanyi_1 (
    .S0(register_1_q[1]), .S1(register_1_q[0]), .in(in_1), .ns0(status_zhuanyi_1_ns1[1]),
    .ns1(status_zhuanyi_1_ns1[0]));
  Register #(.width(2)) register_1 (.D(status_zhuanyi_1_ns1), .Q(register_1_q), .clk(clock_1_out));  // open: en, clr
  Demultiplexer #(.select(2)) demultiplexer_1 (
    .out0(out_3), .out1(out_4), .out2(out_5), .out3(out_6), .in(1'b1), .sel(status_zhuanyi_1_ns1));  // open: en

  assign s0 = 1'b0;
endmodule

module tes (
  output out_1,
  output out_2,
  output out_3,
  output out_4,
  output out_5,
  output out_6,
  output out_7
);

  wire clock_1_out;
  wire [7:0] counter_1_q;

  Clock clock_1 (.out(clock_1_out));
  Counter counter_1 (.Q(counter_1_q), .carry(out_7), .clk(clock_1_out));  // open: load, D, count, clr
  ROM #(.dataWidth(1)) rom_1 (.addr(counter_1_q), .data(out_1));  // open: sel
  mod5 mod5_1 (.in_1(out_1), .s0(out_2), .out_3(out_3), .out_4(out_4), .out_5(out_5), .out_6(out_6));

  // Notes on the sheet:
  //   contents of rom_1 (hex, n*v repeats v):
  //   0 1 0 0 1 0 0 1
endmodule

module status_zhuanyi (
  input  S0,
  input  S1,
  input  in,
  output ns0,
  output ns1
);

  wire and_1_out, and_2_out, and_3_out, and_4_out, and_5_out, and_6_out, not_1_out, not_2_out, not_3_out,
       not_4_out, not_5_out, not_6_out, not_7_out, not_8_out;

  not not_1 (not_1_out, S0);
  not not_2 (not_2_out, S1);
  not not_3 (not_3_out, S0);
  not not_4 (not_4_out, S1);
  not not_5 (not_5_out, S0);
  not not_6 (not_6_out, in);
  not not_7 (not_7_out, S1);
  not not_8 (not_8_out, in);
  and and_1 (and_1_out, not_1_out, S1);
  and and_2 (and_2_out, S0, not_2_out);
  and and_3 (and_3_out, not_3_out, not_4_out, in);
  and and_4 (and_4_out, not_5_out, S1, not_6_out);
  and and_5 (and_5_out, S0, not_7_out, not_8_out);
  and and_6 (and_6_out, S0, S1, in);
  or or_1 (ns0, and_1_out, and_2_out);
  or or_2 (ns1, and_3_out, and_4_out, and_5_out, and_6_out);
endmodule
