// Logisim project navigation.circ as structural Verilog: 3 circuits, main circuit navigation
module navigation (
  input  [1:0] dir,
  input  clk,
  input  reset,
  output arrive,
  output hit
);

  wire not_1_out, status_cunchu_1_s10, status_cunchu_1_s11, status_cunchu_1_s12, status_cunchu_2_s10,
       status_cunchu_2_s11, status_cunchu_2_s12, status_zhuanyi_1_arrive, status_zhuanyi_1_hit,
       status_zhuanyi_1_s0, status_zhuanyi_1_s1, status_zhuanyi_1_s2;

  status_zhuanyi status_zhuanyi_1 (
    .S10(status_cunchu_2_s10), .S11(status_cunchu_2_s11), .S12(status_cunchu_2_s12), .dir0(dir[1]),
    .dir1(dir[0]), .S0(status_zhuanyi_1_s0), .S1(status_zhuanyi_1_s1), .S2(status_zhuanyi_1_s2),
    .hit(status_zhuanyi_1_hit), .arrive(status_zhuanyi_1_arrive));
  status_cunchu status_cunchu_1 (
    .S0(status_zhuanyi_1_s0), .S1(status_zhuanyi_1_s1), .S2(status_zhuanyi_1_s2), .clk(clk), .reset(reset),
    .S10(status_cunchu_1_s10), .S11(status_cunchu_1_s11), .S12(status_cunchu_1_s12));
  not not_1 (not_1_out, clk);
  status_cunchu status_cunchu_2 (
    .S0(status_cunchu_1_s10), .S1(status_cunchu_1_s11), .S2(status_cunchu_1_s12), .clk(not_1_out),
    .reset(reset), .S10(status_cunchu_2_s10), .S11(status_cunchu_2_s11), .S12(status_cunchu_2_s12));
  Register #(.width(1)) register_1 (.D(status_zhuanyi_1_arrive), .Q(arrive), .clk(clk), .clr(reset));  // open: en
  Register #(.width(1)) register_2 (.D(status_zhuanyi_1_hit), .Q(hit), .clk(clk), .clr(reset));  // open: en
endmodule

module status_cunchu (
  input  S0,
  input  S1,
  input  S2,
  input  clk,
  input  reset,
  output S10,
  output S11,
  output S12
);

  Register #(.width(3)) register_1 (.D({S0, S1, S2}), .Q({S10, S11, S12}), .clk(clk), .clr(reset));  // open: en
endmodule

module status_zhuanyi (
  input  S10,
  input  S11,
  input  S12,
  input  dir0,
  input  dir1,
  output S0,
  output S1,
  output S2,
  output hit,
  output arrive
);

  wire and_1_out, and_2_out, and_3_out, and_4_out, and_5_out, and_6_out, and_7_out, and_8_out, and_9_out,
       and_10_out, and_11_out, and_12_out, and_13_out, and_14_out, and_15_out, and_16_out, and_17_out,
       not_1_out, not_2_out, not_3_out, not_4_out, not_5_out, not_6_out, not_7_out, not_8_out, not_9_out,
       not_10_out, not_11_out, not_12_out, not_13_out, not_14_out, not_15_out, not_16_out, not_17_out,
       not_18_out, not_19_out, not_20_out, not_21_out, not_22_out, not_23_out, not_24_out, not_25_out,
       not_26_out, not_27_out, not_28_out, not_29_out, not_30_out, not_31_out, not_32_out;

  not not_1 (not_1_out, S12);
  not not_2 (not_2_out, dir0);
  not not_3 (not_3_out, dir1);
  not not_4 (not_4_out, dir0);
  not not_5 (not_5_out, S11);
  not not_6 (not_6_out, dir0);
  not not_7 (not_7_out, dir0);
  not not_8 (not_8_out, dir1);
  not not_9 (not_9_out, S12);
  not not_10 (not_10_out, dir0);
  not not_11 (not_11_out, S12);
  not not_12 (not_12_out, dir1);
  not not_13 (not_13_out, S10);
  not not_14 (not_14_out, S11);
  not not_15 (not_15_out, dir0);
  not not_16 (not_16_out, dir1);
  not not_17 (not_17_out, dir1);
  not not_18 (not_18_out, S10);
  not not_19 (not_19_out, S12);
  not not_20 (not_20_out, dir0);
  not not_21 (not_21_out, S10);
  not not_22 (not_22_out, S11);
  not not_23 (not_23_out, S12);
  not not_24 (not_24_out, S10);
  not not_25 (not_25_out, S12);
  not not_26 (not_26_out, dir1);
  not not_27 (not_27_out, dir0);
  not not_28 (not_28_out, dir1);
  not not_29 (not_29_out, S12);
  not not_30 (not_30_out, dir0);
  not not_31 (not_31_out, dir1);
  not not_32 (not_32_out, dir0);
  and and_1 (and_1_out, S11, not_1_out, not_2_out, not_3_out);
  and and_2 (and_2_out, S11, S12, not_4_out, dir1);
  and and_3 (and_3_out, not_5_out, S12, not_6_out);
  and and_4 (and_4_out, S12, not_7_out, not_8_out);
  and and_5 (and_5_out, S11, not_9_out, not_10_out, dir1);
  and and_6 (and_6_out, S11, not_11_out, dir0, not_12_out);
  and and_7 (and_7_out, S11, S12, dir0, dir1);
  and and_8 (and_8_out, not_13_out, not_14_out, not_15_out, not_16_out);
  and and_9 (and_9_out, S11, dir0, dir1);
  and and_10 (and_10_out, S11, S12, not_17_out);
  and and_11 (and_11_out, not_18_out, not_19_out, not_20_out, dir1);
  and and_12 (and_12_out, not_21_out, not_22_out, not_23_out, dir0);
  and and_13 (and_13_out, not_24_out, not_25_out, dir0, not_26_out);
  and and_14 (and_14_out, S12, dir0, dir1);
  and and_15 (and_15_out, S11, S12, not_27_out, not_28_out);
  and and_16 (and_16_out, S11, not_29_out, not_30_out, not_31_out);
  and and_17 (and_17_out, S11, S12, not_32_out, dir1);
  or or_1 (S0, and_1_out, and_2_out);
  or or_2 (S1, and_3_out, and_4_out, and_5_out, and_6_out, and_7_out);
  or or_3 (S2, and_8_out, and_9_out, and_10_out);
  or or_4 (hit, and_11_out, and_12_out, and_13_out, and_14_out, and_15_out);
  or or_5 (arrive, and_16_out, and_17_out);
endmodule
